// Logisim project 2024-1-Trabalho Final (ULA).circ as structural Verilog: 24 circuits, main circuit main
module main (
  input  [2:0] Sel_OP,
  input  Escreve,
  input  [7:0] Insere_Valor,
  input  sel_Valor,
  input  [1:0] Sel_RW,
  input  [1:0] Sel_RA,
  input  [1:0] Sel_RB,
  output [7:0] S,
  output Z,
  output C
);

  wire bcd_to_7_segment_decoder_1_p1, bcd_to_7_segment_decoder_1_p2, bcd_to_7_segment_decoder_1_p3,
       bcd_to_7_segment_decoder_1_p4, bcd_to_7_segment_decoder_1_p5, bcd_to_7_segment_decoder_1_p6,
       bcd_to_7_segment_decoder_1_p7, bcd_to_7_segment_decoder_1_p8, bcd_to_7_segment_decoder_2_p1,
       bcd_to_7_segment_decoder_2_p2, bcd_to_7_segment_decoder_2_p3, bcd_to_7_segment_decoder_2_p4,
       bcd_to_7_segment_decoder_2_p5, bcd_to_7_segment_decoder_2_p6, bcd_to_7_segment_decoder_2_p7,
       bcd_to_7_segment_decoder_2_p8, bcd_to_7_segment_decoder_3_p1, bcd_to_7_segment_decoder_3_p2,
       bcd_to_7_segment_decoder_3_p3, bcd_to_7_segment_decoder_3_p4, bcd_to_7_segment_decoder_3_p6,
       bcd_to_7_segment_decoder_3_p7, bcd_to_7_segment_decoder_3_p8, binary_to_bcd_converter_1_p4;
  wire [7:0] banco_de_registradores_1_va, banco_de_registradores_1_vb, mux_2_to_1_8b_1_vw;

  _7_Segment_Display u_7_segment_display_1 (
    .g(bcd_to_7_segment_decoder_1_p1), .f(bcd_to_7_segment_decoder_1_p3), .a(bcd_to_7_segment_decoder_1_p6),
    .b(bcd_to_7_segment_decoder_1_p8), .e(bcd_to_7_segment_decoder_1_p2), .d(bcd_to_7_segment_decoder_1_p4),
    .c(bcd_to_7_segment_decoder_1_p7));  // open: dp
  // BCD_to_7_Segment_decoder bcd_to_7_segment_decoder_1: pin names not known; wires that end beside it: bcd_to_7_segment_decoder_1_p1, bcd_to_7_segment_decoder_1_p2, bcd_to_7_segment_decoder_1_p3, bcd_to_7_segment_decoder_1_p4, bcd_to_7_segment_decoder_1_p5, bcd_to_7_segment_decoder_1_p6, bcd_to_7_segment_decoder_1_p7, bcd_to_7_segment_decoder_1_p8
  _7_Segment_Display u_7_segment_display_2 (
    .g(bcd_to_7_segment_decoder_2_p1), .f(bcd_to_7_segment_decoder_2_p3), .a(bcd_to_7_segment_decoder_2_p6),
    .b(bcd_to_7_segment_decoder_2_p8), .e(bcd_to_7_segment_decoder_2_p2), .d(bcd_to_7_segment_decoder_2_p4),
    .c(bcd_to_7_segment_decoder_2_p7));  // open: dp
  // BCD_to_7_Segment_decoder bcd_to_7_segment_decoder_2: pin names not known; wires that end beside it: bcd_to_7_segment_decoder_2_p1, bcd_to_7_segment_decoder_2_p2, bcd_to_7_segment_decoder_2_p3, bcd_to_7_segment_decoder_2_p4, bcd_to_7_segment_decoder_2_p5, bcd_to_7_segment_decoder_2_p6, bcd_to_7_segment_decoder_2_p7, bcd_to_7_segment_decoder_2_p8
  // Binary_to_BCD_converter #(.binvalue(8)) binary_to_bcd_converter_1: pin names not known; wires that end beside it: S, bcd_to_7_segment_decoder_1_p5, bcd_to_7_segment_decoder_2_p5, binary_to_bcd_converter_1_p4
  _7_Segment_Display u_7_segment_display_3 (
    .g(bcd_to_7_segment_decoder_3_p1), .f(bcd_to_7_segment_decoder_3_p3), .a(bcd_to_7_segment_decoder_3_p6),
    .b(bcd_to_7_segment_decoder_3_p8), .e(bcd_to_7_segment_decoder_3_p2), .d(bcd_to_7_segment_decoder_3_p4),
    .c(bcd_to_7_segment_decoder_3_p7));  // open: dp
  // BCD_to_7_Segment_decoder bcd_to_7_segment_decoder_3: pin names not known; wires that end beside it: bcd_to_7_segment_decoder_3_p1, bcd_to_7_segment_decoder_3_p2, bcd_to_7_segment_decoder_3_p3, bcd_to_7_segment_decoder_3_p4, binary_to_bcd_converter_1_p4, bcd_to_7_segment_decoder_3_p6, bcd_to_7_segment_decoder_3_p7, bcd_to_7_segment_decoder_3_p8
  MUX_2_to_1_8b mux_2_to_1_8b_1 (.Insere_valor(Insere_Valor), .S(S), .Sel_valor(sel_Valor), .VW(mux_2_to_1_8b_1_vw));
  banco_de_registradores banco_de_registradores_1 (
    .escreve(Escreve), .Sel_RW(Sel_RW), .VW(mux_2_to_1_8b_1_vw), .Sel_RA(Sel_RA), .Sel_RB(Sel_RB),
    .VA(banco_de_registradores_1_va), .VB(banco_de_registradores_1_vb));
  ULA_2E_8bit ula_2e_8bit_1 (
    .Sel_OP(Sel_OP), .A(banco_de_registradores_1_va), .B(banco_de_registradores_1_vb), .S(S), .zero_flag(Z),
    .overflow(C));
  LED LEDzero (.in(Z));
  LED LED_OF (.in(C));
  LED led_1 (.in(S[7]));
  LED led_2 (.in(S[6]));
  LED led_3 (.in(S[5]));
  LED led_4 (.in(S[4]));
  LED led_5 (.in(S[3]));
  LED led_6 (.in(S[2]));
  LED led_7 (.in(S[1]));
  LED led_8 (.in(S[0]));

  // Notes on the sheet:
  //   128 | 64 | 32 | 16 | 8 | 4 | 2 | 1
  //   Seleciona o valor a ser inserido no registrador
  //   (1= insere | 0 = S)
  //   (ativa na transição de subida)
  //   Comando para escrever no registrador
  //    Seleciona a operação da ULA:
  //   000 = A OR B | 001 =  A - B | 010 = A + B | 011 =  A * B|
  //   100 = A XOR B | 101 = ~B | 110  = A / B | 111 A AND B
  //   Seleciona qual registrador será escrito (00 = R0 | 01 = R1 | 10 = R2 | 11 = R3)
  //   Seleciona o registrador para saída VA (00 = R0 | 01 = R1 | 10 = R2 | 11 = R3)
  //   Seleciona o registrador para saída VB (00 = R0 | 01 = R1 | 10 = R2 | 11 = R3)
  //    Saída de 8 bits da ULA
  //   (1 = Zero | 0 = Não Zero)
  //   Indicador de resultado zero
  //   Indicador de overflow/underflow
  //   (1 = Overflow | 0 = Não Overflow/Underflow)
endmodule

module registrador_8b (
  input  [7:0] entrada,
  input  escreve,
  output [7:0] saida
);

  D_Flip_Flop d_ff_1 (.D(entrada[0]), .clk(escreve), .Q(saida[0]));  // open: Qn, preset, reset
  D_Flip_Flop d_ff_2 (.D(entrada[1]), .clk(escreve), .Q(saida[1]));  // open: Qn, preset, reset
  D_Flip_Flop d_ff_3 (.D(entrada[2]), .clk(escreve), .Q(saida[2]));  // open: Qn, preset, reset
  D_Flip_Flop d_ff_4 (.D(entrada[3]), .clk(escreve), .Q(saida[3]));  // open: Qn, preset, reset
  D_Flip_Flop d_ff_5 (.D(entrada[4]), .clk(escreve), .Q(saida[4]));  // open: Qn, preset, reset
  D_Flip_Flop d_ff_6 (.D(entrada[5]), .clk(escreve), .Q(saida[5]));  // open: Qn, preset, reset
  D_Flip_Flop d_ff_7 (.D(entrada[6]), .clk(escreve), .Q(saida[6]));  // open: Qn, preset, reset
  D_Flip_Flop d_ff_8 (.D(entrada[7]), .clk(escreve), .Q(saida[7]));  // open: Qn, preset, reset
endmodule

module banco_de_registradores (
  input  escreve,
  input  [1:0] Sel_RW,
  input  [7:0] VW,
  input  [1:0] Sel_RA,
  input  [1:0] Sel_RB,
  output [7:0] VA,
  output [7:0] VB
);

  wire dmux_1_to_4_1b_1_r0, dmux_1_to_4_1b_1_r1, dmux_1_to_4_1b_1_r2, dmux_1_to_4_1b_1_r3;
  wire [7:0] dmux_1_to_4_8b_1_r0, dmux_1_to_4_8b_1_r1, dmux_1_to_4_8b_1_r2, dmux_1_to_4_8b_1_r3,
       registrador_8b_1_saida, registrador_8b_2_saida, registrador_8b_3_saida, registrador_8b_4_saida;

  DMUX_1_to_4_1b dmux_1_to_4_1b_1 (
    .S1(Sel_RW[1]), .S0(Sel_RW[0]), .Entrada(escreve), .R0(dmux_1_to_4_1b_1_r0), .R1(dmux_1_to_4_1b_1_r1),
    .R2(dmux_1_to_4_1b_1_r2), .R3(dmux_1_to_4_1b_1_r3));
  DMUX_1_to_4_8b dmux_1_to_4_8b_1 (
    .Sel_RW(Sel_RW), .VW(VW), .R0(dmux_1_to_4_8b_1_r0), .R1(dmux_1_to_4_8b_1_r1), .R2(dmux_1_to_4_8b_1_r2),
    .R3(dmux_1_to_4_8b_1_r3));
  registrador_8b registrador_8b_1 (
    .entrada(dmux_1_to_4_8b_1_r0), .escreve(dmux_1_to_4_1b_1_r0), .saida(registrador_8b_1_saida));
  registrador_8b registrador_8b_2 (
    .entrada(dmux_1_to_4_8b_1_r1), .escreve(dmux_1_to_4_1b_1_r1), .saida(registrador_8b_2_saida));
  registrador_8b registrador_8b_3 (
    .entrada(dmux_1_to_4_8b_1_r2), .escreve(dmux_1_to_4_1b_1_r2), .saida(registrador_8b_3_saida));
  registrador_8b registrador_8b_4 (
    .entrada(dmux_1_to_4_8b_1_r3), .escreve(dmux_1_to_4_1b_1_r3), .saida(registrador_8b_4_saida));
  MUX_4_to_1_8b mux_4_to_1_8b_1 (
    .R0(registrador_8b_1_saida), .R1(registrador_8b_2_saida), .R2(registrador_8b_3_saida),
    .R3(registrador_8b_4_saida), .Sel_R(Sel_RA), .VAB(VA));
  MUX_4_to_1_8b mux_4_to_1_8b_2 (
    .R0(registrador_8b_1_saida), .R1(registrador_8b_2_saida), .R2(registrador_8b_3_saida),
    .R3(registrador_8b_4_saida), .Sel_R(Sel_RB), .VAB(VB));
endmodule

module MUX_2_to_1_1b (
  input  Sel_valor,
  input  Insere,
  input  S,
  output VW
);

  wire and_1_out, and_2_out, not_1_out;

  not not_1 (not_1_out, Sel_valor);
  and and_1 (and_1_out, Insere, Sel_valor);
  and and_2 (and_2_out, S, not_1_out);
  or or_1 (VW, and_1_out, and_2_out);
endmodule

module MUX_2_to_1_8b (
  input  [7:0] Insere_valor,
  input  [7:0] S,
  input  Sel_valor,
  output [7:0] VW
);

  MUX_2_to_1_1b mux_2_to_1_1b_1 (.Insere(Insere_valor[0]), .S(S[0]), .Sel_valor(Sel_valor), .VW(VW[0]));
  MUX_2_to_1_1b mux_2_to_1_1b_2 (.Insere(Insere_valor[1]), .S(S[1]), .Sel_valor(Sel_valor), .VW(VW[1]));
  MUX_2_to_1_1b mux_2_to_1_1b_3 (.Insere(Insere_valor[2]), .S(S[2]), .Sel_valor(Sel_valor), .VW(VW[2]));
  MUX_2_to_1_1b mux_2_to_1_1b_4 (.Insere(Insere_valor[3]), .S(S[3]), .Sel_valor(Sel_valor), .VW(VW[3]));
  MUX_2_to_1_1b mux_2_to_1_1b_5 (.Insere(Insere_valor[4]), .S(S[4]), .Sel_valor(Sel_valor), .VW(VW[4]));
  MUX_2_to_1_1b mux_2_to_1_1b_6 (.Insere(Insere_valor[5]), .S(S[5]), .Sel_valor(Sel_valor), .VW(VW[5]));
  MUX_2_to_1_1b mux_2_to_1_1b_7 (.Insere(Insere_valor[6]), .S(S[6]), .Sel_valor(Sel_valor), .VW(VW[6]));
  MUX_2_to_1_1b mux_2_to_1_1b_8 (.Insere(Insere_valor[7]), .S(S[7]), .Sel_valor(Sel_valor), .VW(VW[7]));
endmodule

module MUX_3_to_1_1b (
  input  ENA,
  input  ENB,
  input  ENC,
  input  A,
  input  B,
  input  C,
  output out_7
);

  wire nand_1_out, nand_2_out, nand_3_out;

  nand nand_1 (nand_1_out, A, ENA);
  nand nand_2 (nand_2_out, B, ENB);
  nand nand_3 (nand_3_out, C, ENC);
  nand nand_4 (out_7, nand_1_out, nand_2_out, nand_3_out);
endmodule

// MUX1b
module MUX_4_to_1_1b (
  input  S1,
  input  S0,
  input  R0,
  input  R1,
  input  R2,
  input  R3,
  output oneBit
);

  wire and_1_out, and_2_out, and_3_out, and_4_out, not_1_out, not_2_out;

  not not_1 (not_1_out, S1);
  not not_2 (not_2_out, S0);
  and and_1 (and_1_out, not_2_out, not_1_out, R0);
  and and_2 (and_2_out, not_1_out, S0, R1);
  and and_3 (and_3_out, not_2_out, S1, R2);
  and and_4 (and_4_out, S0, S1, R3);
  or or_1 (oneBit, and_1_out, and_2_out, and_3_out, and_4_out);
endmodule

module MUX_4_to_1_3sel_1b (
  input  [2:0] Sel_op,
  input  Sub_001,
  input  Sum_010,
  input  Mult_011,
  input  Div_110,
  output out_6
);

  wire and_1_out, and_2_out, and_3_out, and_4_out, not_1_out, not_2_out, not_3_out;

  not not_1 (not_1_out, Sel_op[2]);
  not not_2 (not_2_out, Sel_op[1]);
  not not_3 (not_3_out, Sel_op[0]);
  and and_1 (and_1_out, not_1_out, not_2_out, Sel_op[0], Sub_001);
  and and_2 (and_2_out, not_1_out, Sel_op[1], not_3_out, Sum_010);
  and and_3 (and_3_out, not_1_out, Sel_op[1], Sel_op[0], Mult_011);
  and and_4 (and_4_out, Sel_op[2], Sel_op[1], not_3_out, Div_110);
  or or_1 (out_6, and_1_out, and_2_out, and_3_out, and_4_out);
endmodule

module MUX_4_to_1_8b (
  input  [7:0] R0,
  input  [7:0] R1,
  input  [7:0] R2,
  input  [7:0] R3,
  input  [1:0] Sel_R,
  output [7:0] VAB
);

  MUX_4_to_1_1b mux_4_to_1_1b_1 (
    .R0(R0[0]), .R1(R1[0]), .R2(R2[0]), .R3(R3[0]), .S1(Sel_R[1]), .S0(Sel_R[0]), .oneBit(VAB[0]));
  MUX_4_to_1_1b mux_4_to_1_1b_2 (
    .R0(R0[1]), .R1(R1[1]), .R2(R2[1]), .R3(R3[1]), .S1(Sel_R[1]), .S0(Sel_R[0]), .oneBit(VAB[1]));
  MUX_4_to_1_1b mux_4_to_1_1b_3 (
    .R0(R0[2]), .R1(R1[2]), .R2(R2[2]), .R3(R3[2]), .S1(Sel_R[1]), .S0(Sel_R[0]), .oneBit(VAB[2]));
  MUX_4_to_1_1b mux_4_to_1_1b_4 (
    .R0(R0[3]), .R1(R1[3]), .R2(R2[3]), .R3(R3[3]), .S1(Sel_R[1]), .S0(Sel_R[0]), .oneBit(VAB[3]));
  MUX_4_to_1_1b mux_4_to_1_1b_5 (
    .R0(R0[4]), .R1(R1[4]), .R2(R2[4]), .R3(R3[4]), .S1(Sel_R[1]), .S0(Sel_R[0]), .oneBit(VAB[4]));
  MUX_4_to_1_1b mux_4_to_1_1b_6 (
    .R0(R0[5]), .R1(R1[5]), .R2(R2[5]), .R3(R3[5]), .S1(Sel_R[1]), .S0(Sel_R[0]), .oneBit(VAB[5]));
  MUX_4_to_1_1b mux_4_to_1_1b_7 (
    .R0(R0[6]), .R1(R1[6]), .R2(R2[6]), .R3(R3[6]), .S1(Sel_R[1]), .S0(Sel_R[0]), .oneBit(VAB[6]));
  MUX_4_to_1_1b mux_4_to_1_1b_8 (
    .R0(R0[7]), .R1(R1[7]), .R2(R2[7]), .R3(R3[7]), .S1(Sel_R[1]), .S0(Sel_R[0]), .oneBit(VAB[7]));
endmodule

// MUX 1b
module MUX_8_to_1_1b (
  input  S0,
  input  S1,
  input  S2,
  input  in_4,
  input  in_5,
  input  in_6,
  input  in_7,
  input  in_8,
  input  in_9,
  input  in_10,
  input  in_11,
  output out_12
);

  wire and_1_out, and_2_out, and_3_out, and_4_out, and_5_out, and_6_out, and_7_out, and_8_out, not_1_out,
       not_2_out, not_3_out;

  not not_1 (not_1_out, S2);
  not not_2 (not_2_out, S1);
  not not_3 (not_3_out, S0);
  and and_1 (and_1_out, in_4, not_3_out, not_2_out, not_1_out);
  and and_2 (and_2_out, in_5, not_3_out, not_2_out, S2);
  and and_3 (and_3_out, in_6, not_3_out, S1, not_1_out);
  and and_4 (and_4_out, in_7, not_3_out, S1, S2);
  and and_5 (and_5_out, in_8, S0, not_2_out, not_1_out);
  and and_6 (and_6_out, in_9, S0, not_2_out, S2);
  and and_7 (and_7_out, in_10, S0, S1, not_1_out);
  and and_8 (and_8_out, in_11, S0, S1, S2);
  or or_1 (out_12, and_1_out, and_2_out, and_3_out, and_4_out, and_5_out, and_6_out, and_7_out, and_8_out);
endmodule

module MUX_8_to_1_8b (
  input  [7:0] ou,
  input  [7:0] sub,
  input  [7:0] adi,
  input  [7:0] mult,
  input  [7:0] ex_or,
  input  [7:0] bar,
  input  [7:0] div,
  input  [7:0] e,
  input  [2:0] Sel_OP,
  output [7:0] out_10
);

  MUX_8_to_1_1b mux_8_to_1_1b_1 (
    .in_4(ou[0]), .in_5(sub[0]), .in_6(adi[0]), .in_7(mult[0]), .in_8(ex_or[0]), .in_9(bar[0]),
    .in_10(div[0]), .in_11(e[0]), .S0(Sel_OP[2]), .S1(Sel_OP[1]), .S2(Sel_OP[0]), .out_12(out_10[0]));
  MUX_8_to_1_1b mux_8_to_1_1b_2 (
    .in_4(ou[1]), .in_5(sub[1]), .in_6(adi[1]), .in_7(mult[1]), .in_8(ex_or[1]), .in_9(bar[1]),
    .in_10(div[1]), .in_11(e[1]), .S0(Sel_OP[2]), .S1(Sel_OP[1]), .S2(Sel_OP[0]), .out_12(out_10[1]));
  MUX_8_to_1_1b mux_8_to_1_1b_3 (
    .in_4(ou[2]), .in_5(sub[2]), .in_6(adi[2]), .in_7(mult[2]), .in_8(ex_or[2]), .in_9(bar[2]),
    .in_10(div[2]), .in_11(e[2]), .S0(Sel_OP[2]), .S1(Sel_OP[1]), .S2(Sel_OP[0]), .out_12(out_10[2]));
  MUX_8_to_1_1b mux_8_to_1_1b_4 (
    .in_4(ou[3]), .in_5(sub[3]), .in_6(adi[3]), .in_7(mult[3]), .in_8(ex_or[3]), .in_9(bar[3]),
    .in_10(div[3]), .in_11(e[3]), .S0(Sel_OP[2]), .S1(Sel_OP[1]), .S2(Sel_OP[0]), .out_12(out_10[3]));
  MUX_8_to_1_1b mux_8_to_1_1b_5 (
    .in_4(ou[4]), .in_5(sub[4]), .in_6(adi[4]), .in_7(mult[4]), .in_8(ex_or[4]), .in_9(bar[4]),
    .in_10(div[4]), .in_11(e[4]), .S0(Sel_OP[2]), .S1(Sel_OP[1]), .S2(Sel_OP[0]), .out_12(out_10[4]));
  MUX_8_to_1_1b mux_8_to_1_1b_6 (
    .in_4(ou[5]), .in_5(sub[5]), .in_6(adi[5]), .in_7(mult[5]), .in_8(ex_or[5]), .in_9(bar[5]),
    .in_10(div[5]), .in_11(e[5]), .S0(Sel_OP[2]), .S1(Sel_OP[1]), .S2(Sel_OP[0]), .out_12(out_10[5]));
  MUX_8_to_1_1b mux_8_to_1_1b_7 (
    .in_4(ou[6]), .in_5(sub[6]), .in_6(adi[6]), .in_7(mult[6]), .in_8(ex_or[6]), .in_9(bar[6]),
    .in_10(div[6]), .in_11(e[6]), .S0(Sel_OP[2]), .S1(Sel_OP[1]), .S2(Sel_OP[0]), .out_12(out_10[6]));
  MUX_8_to_1_1b mux_8_to_1_1b_8 (
    .in_4(ou[7]), .in_5(sub[7]), .in_6(adi[7]), .in_7(mult[7]), .in_8(ex_or[7]), .in_9(bar[7]),
    .in_10(div[7]), .in_11(e[7]), .S0(Sel_OP[2]), .S1(Sel_OP[1]), .S2(Sel_OP[0]), .out_12(out_10[7]));
endmodule

module DMUX_1_to_4_1b (
  input  S1,
  input  S0,
  input  Entrada,
  output R0,
  output R1,
  output R2,
  output R3
);

  wire not_1_out, not_2_out;

  not not_1 (not_1_out, S1);
  not not_2 (not_2_out, S0);
  and and_1 (R0, not_1_out, not_2_out, Entrada);
  and and_2 (R1, not_1_out, S0, Entrada);
  and and_3 (R2, S1, not_2_out, Entrada);
  and and_4 (R3, S1, S0, Entrada);
endmodule

module DMUX_1_to_4_8b (
  input  [1:0] Sel_RW,
  input  [7:0] VW,
  output [7:0] R0,
  output [7:0] R1,
  output [7:0] R2,
  output [7:0] R3
);

  DMUX_1_to_4_1b dmux_1_to_4_1b_1 (
    .S1(Sel_RW[1]), .S0(Sel_RW[0]), .Entrada(VW[0]), .R0(R0[0]), .R1(R1[0]), .R2(R2[0]), .R3(R3[0]));
  DMUX_1_to_4_1b dmux_1_to_4_1b_2 (
    .S1(Sel_RW[1]), .S0(Sel_RW[0]), .Entrada(VW[1]), .R0(R0[1]), .R1(R1[1]), .R2(R2[1]), .R3(R3[1]));
  DMUX_1_to_4_1b dmux_1_to_4_1b_3 (
    .S1(Sel_RW[1]), .S0(Sel_RW[0]), .Entrada(VW[2]), .R0(R0[2]), .R1(R1[2]), .R2(R2[2]), .R3(R3[2]));
  DMUX_1_to_4_1b dmux_1_to_4_1b_4 (
    .S1(Sel_RW[1]), .S0(Sel_RW[0]), .Entrada(VW[3]), .R0(R0[3]), .R1(R1[3]), .R2(R2[3]), .R3(R3[3]));
  DMUX_1_to_4_1b dmux_1_to_4_1b_5 (
    .S1(Sel_RW[1]), .S0(Sel_RW[0]), .Entrada(VW[4]), .R0(R0[4]), .R1(R1[4]), .R2(R2[4]), .R3(R3[4]));
  DMUX_1_to_4_1b dmux_1_to_4_1b_6 (
    .S1(Sel_RW[1]), .S0(Sel_RW[0]), .Entrada(VW[5]), .R0(R0[5]), .R1(R1[5]), .R2(R2[5]), .R3(R3[5]));
  DMUX_1_to_4_1b dmux_1_to_4_1b_7 (
    .S1(Sel_RW[1]), .S0(Sel_RW[0]), .Entrada(VW[6]), .R0(R0[6]), .R1(R1[6]), .R2(R2[6]), .R3(R3[6]));
  DMUX_1_to_4_1b dmux_1_to_4_1b_8 (
    .S1(Sel_RW[1]), .S0(Sel_RW[0]), .Entrada(VW[7]), .R0(R0[7]), .R1(R1[7]), .R2(R2[7]), .R3(R3[7]));
endmodule

module or_8b (
  input  [7:0] A,
  input  [7:0] B,
  output [7:0] or_result
);

  or or_1 (or_result[0], A[0], B[0]);
  or or_2 (or_result[1], A[1], B[1]);
  or or_3 (or_result[2], A[2], B[2]);
  or or_4 (or_result[3], A[3], B[3]);
  or or_5 (or_result[4], A[4], B[4]);
  or or_6 (or_result[5], A[5], B[5]);
  or or_7 (or_result[6], A[6], B[6]);
  or or_8 (or_result[7], A[7], B[7]);
endmodule

module sub_8b (
  input  [7:0] A,
  input  [7:0] B,
  output [7:0] sub_result,
  output Overflow
);

  wire fulladder_1_ci, fulladder_2_ci, fulladder_3_ci, fulladder_4_ci, fulladder_5_ci, fulladder_6_ci,
       fulladder_7_ci, fulladder_8_ci, not_1_out, not_2_out, not_3_out, not_4_out, not_5_out, not_6_out,
       not_7_out, not_8_out;

  fullAdder fulladder_1 (.ci(fulladder_1_ci), .A(A[0]), .B(not_1_out), .s(sub_result[0]), .C(1'b1));
  not not_1 (not_1_out, B[0]);
  fullAdder fulladder_2 (.ci(fulladder_2_ci), .A(A[1]), .B(not_2_out), .s(sub_result[1]), .C(fulladder_1_ci));
  not not_2 (not_2_out, B[1]);
  fullAdder fulladder_3 (.ci(fulladder_3_ci), .A(A[2]), .B(not_3_out), .s(sub_result[2]), .C(fulladder_2_ci));
  not not_3 (not_3_out, B[2]);
  fullAdder fulladder_4 (.ci(fulladder_4_ci), .A(A[3]), .B(not_4_out), .s(sub_result[3]), .C(fulladder_3_ci));
  not not_4 (not_4_out, B[3]);
  fullAdder fulladder_5 (.ci(fulladder_5_ci), .A(A[4]), .B(not_5_out), .s(sub_result[4]), .C(fulladder_4_ci));
  not not_5 (not_5_out, B[4]);
  fullAdder fulladder_6 (.ci(fulladder_6_ci), .A(A[5]), .B(not_6_out), .s(sub_result[5]), .C(fulladder_5_ci));
  not not_6 (not_6_out, B[5]);
  fullAdder fulladder_7 (.ci(fulladder_7_ci), .A(A[6]), .B(not_7_out), .s(sub_result[6]), .C(fulladder_6_ci));
  not not_7 (not_7_out, B[6]);
  fullAdder fulladder_8 (.ci(fulladder_8_ci), .A(A[7]), .B(not_8_out), .s(sub_result[7]), .C(fulladder_7_ci));
  not not_8 (not_8_out, B[7]);
  xor xor_1 (Overflow, fulladder_7_ci, fulladder_8_ci);
endmodule

module sum_8b (
  input  [7:0] A,
  input  [7:0] B,
  output [7:0] sum_result,
  output Overflow
);

  wire fulladder_1_ci, fulladder_2_ci, fulladder_3_ci, fulladder_4_ci, fulladder_5_ci, fulladder_6_ci,
       fulladder_7_ci, ha_ci;

  half_adder ha (.ci(ha_ci), .A(A[0]), .B(B[0]), .s(sum_result[0]));
  fullAdder fulladder_1 (.ci(fulladder_1_ci), .A(A[1]), .B(B[1]), .s(sum_result[1]), .C(ha_ci));
  fullAdder fulladder_2 (.ci(fulladder_2_ci), .A(A[2]), .B(B[2]), .s(sum_result[2]), .C(fulladder_1_ci));
  fullAdder fulladder_3 (.ci(fulladder_3_ci), .A(A[3]), .B(B[3]), .s(sum_result[3]), .C(fulladder_2_ci));
  fullAdder fulladder_4 (.ci(fulladder_4_ci), .A(A[4]), .B(B[4]), .s(sum_result[4]), .C(fulladder_3_ci));
  fullAdder fulladder_5 (.ci(fulladder_5_ci), .A(A[5]), .B(B[5]), .s(sum_result[5]), .C(fulladder_4_ci));
  fullAdder fulladder_6 (.ci(fulladder_6_ci), .A(A[6]), .B(B[6]), .s(sum_result[6]), .C(fulladder_5_ci));
  fullAdder fulladder_7 (.ci(fulladder_7_ci), .A(A[7]), .B(B[7]), .s(sum_result[7]), .C(fulladder_6_ci));
  xor xor_1 (Overflow, fulladder_6_ci, fulladder_7_ci);
endmodule

module mul_8b (
  input  [7:0] A,
  input  [7:0] B,
  output [7:0] mult_result,
  output Overflow
);

  wire [7:0] multiplier_1_cout;

  Multiplier multiplier_1 (.a(A), .b(B), .out(mult_result), .cin({8{1'b0}}), .cout(multiplier_1_cout));
  or or_1 (Overflow, multiplier_1_cout[0], multiplier_1_cout[1], multiplier_1_cout[2], multiplier_1_cout[3], multiplier_1_cout[4], multiplier_1_cout[5], multiplier_1_cout[6], multiplier_1_cout[7]);
endmodule

module xor_8b (
  input  [7:0] A,
  input  [7:0] B,
  output [7:0] xor_result
);

  xor xor_1 (xor_result[0], A[0], B[0]);
  xor xor_2 (xor_result[1], A[1], B[1]);
  xor xor_3 (xor_result[2], A[2], B[2]);
  xor xor_4 (xor_result[3], A[3], B[3]);
  xor xor_5 (xor_result[4], A[4], B[4]);
  xor xor_6 (xor_result[5], A[5], B[5]);
  xor xor_7 (xor_result[6], A[6], B[6]);
  xor xor_8 (xor_result[7], A[7], B[7]);
endmodule

module neg_B_8b (
  input  [7:0] B,
  output [7:0] b_neg_result
);

  assign b_neg_result = ~B;  // NOT_Gate not_1, 8 bits wide
endmodule

module div_8b (
  input  [7:0] A,
  input  [7:0] B,
  output [7:0] div_result,
  output Overflow
);

  wire [7:0] divider_1_rem;

  Divider divider_1 (.a(A), .b(B), .out(div_result), .upper({8{1'b0}}), .rem(divider_1_rem));
  or or_1 (Overflow, divider_1_rem[0], divider_1_rem[1], divider_1_rem[2], divider_1_rem[3], divider_1_rem[4], divider_1_rem[5], divider_1_rem[6], divider_1_rem[7]);
endmodule

module and_8b (
  input  [7:0] A,
  input  [7:0] B,
  output [7:0] and_result
);

  and and_1 (and_result[0], A[0], B[0]);
  and and_2 (and_result[1], A[1], B[1]);
  and and_3 (and_result[2], A[2], B[2]);
  and and_4 (and_result[3], A[3], B[3]);
  and and_5 (and_result[4], A[4], B[4]);
  and and_6 (and_result[5], A[5], B[5]);
  and and_7 (and_result[6], A[6], B[6]);
  and and_8 (and_result[7], A[7], B[7]);
endmodule

module ULA_2E_8bit (
  input  [2:0] Sel_OP,
  input  [7:0] A,
  input  [7:0] B,
  output [7:0] S,
  output zero_flag,
  output overflow
);

  wire OP_001_overflow, OP_010_overflow, OP_011_overflow, OP_110_overflow;
  wire [7:0] OP_000_or_result, OP_001_sub_result, OP_010_sum_result, OP_011_mult_result, OP_100_xor_result,
       OP_101_b_neg_result, OP_110_div_result, OP_111_and_result;

  or_8b OP_000 (.A(A), .B(B), .or_result(OP_000_or_result));
  sub_8b OP_001 (.A(A), .B(B), .sub_result(OP_001_sub_result), .Overflow(OP_001_overflow));
  sum_8b OP_010 (.A(A), .B(B), .sum_result(OP_010_sum_result), .Overflow(OP_010_overflow));
  mul_8b OP_011 (.A(A), .B(B), .mult_result(OP_011_mult_result), .Overflow(OP_011_overflow));
  xor_8b OP_100 (.A(A), .B(B), .xor_result(OP_100_xor_result));
  neg_B_8b OP_101 (.B(B), .b_neg_result(OP_101_b_neg_result));
  div_8b OP_110 (.A(A), .B(B), .div_result(OP_110_div_result), .Overflow(OP_110_overflow));
  and_8b OP_111 (.A(A), .B(B), .and_result(OP_111_and_result));
  MUX_4_to_1_3sel_1b seletor_overflow (
    .Sel_op(Sel_OP), .Sub_001(OP_001_overflow), .Sum_010(OP_010_overflow), .Mult_011(OP_011_overflow),
    .Div_110(OP_110_overflow), .out_6(overflow));
  MUX_8_to_1_8b seletor_result (
    .ou(OP_000_or_result), .sub(OP_001_sub_result), .adi(OP_010_sum_result), .mult(OP_011_mult_result),
    .ex_or(OP_100_xor_result), .bar(OP_101_b_neg_result), .div(OP_110_div_result), .e(OP_111_and_result),
    .Sel_OP(Sel_OP), .out_10(S));
  nor nor_1 (zero_flag, S[7], S[6], S[5], S[4], S[3], S[2], S[1], S[0]);
endmodule

// fa
module fullAdder (
  input  A,
  input  B,
  input  C,
  output ci,
  output s
);

  wire and_1_out, and_2_out, and_3_out, xor_1_out;

  and and_1 (and_1_out, B, C);
  and and_2 (and_2_out, A, C);
  or or_1 (ci, and_1_out, and_2_out, and_3_out);
  and and_3 (and_3_out, A, B);
  xor xor_1 (xor_1_out, A, B);
  xor xor_2 (s, C, xor_1_out);
endmodule

module half_adder (
  input  A,
  input  B,
  output ci,
  output s
);

  and and_1 (ci, A, B);
  xor xor_1 (s, A, B);
endmodule
