// Digital circuit Contador Gray 3 bits.dig as structural Verilog
module Contador_Gray_3_bits (
  input  clk
);

  wire and_1_out, and_2_out, and_3_out, and_4_out, jk_ff_1_nq, jk_ff_1_q, jk_ff_2_nq, jk_ff_2_q, jk_ff_3_nq,
       jk_ff_3_q, xnor_1_out, xor_1_out;

  xnor xnor_1 (xnor_1_out, jk_ff_2_q, jk_ff_3_q);
  xor xor_1 (xor_1_out, jk_ff_2_q, jk_ff_3_q);
  LED led_1 (.in(jk_ff_3_q));
  JK_FF jk_ff_1 (.J(xnor_1_out), .C(clk), .K(xor_1_out), .Q(jk_ff_1_q), .nQ(jk_ff_1_nq));
  LED led_2 (.in(jk_ff_2_q));
  LED led_3 (.in(jk_ff_1_q));
  and and_1 (and_1_out, jk_ff_1_q, jk_ff_3_nq);
  and and_2 (and_2_out, jk_ff_1_q, jk_ff_3_q);
  JK_FF jk_ff_2 (.J(and_1_out), .C(clk), .K(and_2_out), .Q(jk_ff_2_q), .nQ(jk_ff_2_nq));
  and and_3 (and_3_out, jk_ff_2_q, jk_ff_1_nq);
  and and_4 (and_4_out, jk_ff_1_nq, jk_ff_2_nq);
  JK_FF jk_ff_3 (.J(and_3_out), .C(clk), .K(and_4_out), .Q(jk_ff_3_q), .nQ(jk_ff_3_nq));
endmodule
