// Digital circuit Contador Gray.dig as structural Verilog
module Contador_Gray (
  input  clk
);

  wire jk_ff_1_nq, jk_ff_1_q, jk_ff_2_nq, jk_ff_2_q, jk_ff_3_nq, jk_ff_3_q;

  JK_FF jk_ff_1 (.C(clk), .Q(jk_ff_1_q), .nQ(jk_ff_1_nq));  // open: J, K
  JK_FF jk_ff_2 (.C(clk), .Q(jk_ff_2_q), .nQ(jk_ff_2_nq));  // open: J, K
  JK_FF jk_ff_3 (.C(clk), .Q(jk_ff_3_q), .nQ(jk_ff_3_nq));  // open: J, K
  JK_FF jk_ff_4 (.C(clk));  // open: J, K, Q, nQ
endmodule
