// Digital circuit Contador de Pulso Crescente Assíncrono.dig as structural Verilog
module \Contador_de_Pulso_Crescente_Assíncrono  (
  input  in_1,
  input  clk
);

  wire jk_ff_1_nq, jk_ff_1_q, jk_ff_2_nq, jk_ff_2_q, jk_ff_3_nq, jk_ff_3_q, jk_ff_4_q, not_1_out;

  JK_FF jk_ff_1 (.J(in_1), .C(not_1_out), .K(in_1), .Q(jk_ff_1_q), .nQ(jk_ff_1_nq));
  not not_1 (not_1_out, clk);
  JK_FF jk_ff_2 (.J(in_1), .C(jk_ff_1_nq), .K(in_1), .Q(jk_ff_2_q), .nQ(jk_ff_2_nq));
  JK_FF jk_ff_3 (.J(in_1), .C(jk_ff_2_nq), .K(in_1), .Q(jk_ff_3_q), .nQ(jk_ff_3_nq));
  JK_FF jk_ff_4 (.J(in_1), .C(jk_ff_3_nq), .K(in_1), .Q(jk_ff_4_q));  // open: nQ
  LED led_1 (.in(jk_ff_3_q));
  LED led_2 (.in(jk_ff_4_q));
  LED led_3 (.in(jk_ff_1_q));
  LED led_4 (.in(jk_ff_2_q));
endmodule
