// Digital circuit Contador de Pulso Decrescente.dig as structural Verilog
module Contador_de_Pulso_Decrescente (
  input  _0,
  input  _1,
  input  clk,
  output s2,
  output s0,
  output s1,
  output s3
);

  wire and_1_out, jk_ff_as_1_nq, jk_ff_as_2_nq, jk_ff_as_3_nq, not_1_out;

  not not_1 (not_1_out, clk);
  JK_FF_AS jk_ff_as_1 (.Set(_0), .J(_1), .C(not_1_out), .K(_1), .Clr(and_1_out), .Q(s0), .nQ(jk_ff_as_1_nq));
  JK_FF_AS jk_ff_as_2 (.Set(_0), .J(_1), .C(jk_ff_as_1_nq), .K(_1), .Clr(and_1_out), .Q(s1), .nQ(jk_ff_as_2_nq));
  JK_FF_AS jk_ff_as_3 (.Set(_0), .J(_1), .C(jk_ff_as_2_nq), .K(_1), .Clr(and_1_out), .Q(s2), .nQ(jk_ff_as_3_nq));
  JK_FF_AS jk_ff_as_4 (.Set(_0), .J(_1), .C(jk_ff_as_3_nq), .K(_1), .Clr(and_1_out), .Q(s3));  // open: nQ
  and and_1 (and_1_out, s0, s1, s2, s3);

  // Notes on the sheet:
  //   clk: Hz: 2
endmodule
