// Logisim project memória.circ as structural Verilog: 1 circuit, main circuit main
module main (
  input  in_1,
  input  [7:0] \Endereço ,
  input  RW,
  input  in_4,
  output [7:0] \Saída_de_daods 
);

  wire Clear_out, Clock_out, not_1_out;
  wire [6:0] bit_extender_2_out, keyboard_1_data;
  wire [7:0] bit_extender_1_out, counter_1_q;

  Keyboard keyboard_1 (.clk(Clock_out), .re(in_1), .clr(Clear_out), .data(keyboard_1_data));  // open: avail
  assign bit_extender_1_out = {{1{1'b0}}, keyboard_1_data};  // Bit_Extender bit_extender_1
  Clock Clock (.out(Clock_out));
  Button Clear (.out(Clear_out));
  assign \Saída_de_daods  = RW ? bit_extender_1_out : 8'bz;  // Controlled_Buffer Buffer_controlado
  Counter counter_1 (.D(\Endereço ), .Q(counter_1_q), .clk(Clock_out), .clr(Clear_out));  // open: load, count, carry
  not not_1 (not_1_out, RW);
  RAM ram_1 (
    .addr(counter_1_q), .data(\Saída_de_daods ), .clk(Clock_out), .ld(not_1_out), .clr(Clear_out));  // open: sel
  Bit_Extender #(.out_width(7)) bit_extender_2 (.in(\Saída_de_daods ), .out(bit_extender_2_out));
  TTY tty_1 (.data(bit_extender_2_out), .clk(Clock_out), .we(in_4), .clr(Clear_out));

  // Notes on the sheet:
  //   Memória RAM
endmodule
