// Logisim project Banco de Registrador(2018).circ as structural Verilog: 1 circuit, main circuit main
module main (
  input  [7:0] in_1,
  input  in_2,
  input  [3:0] selecionando_Reg,
  input  in_4,
  input  [3:0] in_5,
  input  clock,
  output [7:0] out_7
);

  wire demultiplexer_1_out0, demultiplexer_1_out1, demultiplexer_1_out2, demultiplexer_1_out3,
       demultiplexer_1_out4, demultiplexer_1_out5, demultiplexer_1_out6, demultiplexer_1_out7,
       demultiplexer_1_out8, demultiplexer_1_out9, demultiplexer_1_out10, demultiplexer_1_out11,
       demultiplexer_1_out12, demultiplexer_1_out13, demultiplexer_1_out14, demultiplexer_1_out15;
  wire [7:0] register_1_q, register_2_q, register_3_q, register_4_q, register_5_q, register_6_q,
       register_7_q, register_8_q, register_9_q, register_10_q, register_11_q, register_12_q, register_13_q,
       register_14_q, register_15_q, register_16_q;

  Demultiplexer #(.select(4)) demultiplexer_1 (
    .out0(demultiplexer_1_out0), .out1(demultiplexer_1_out1), .out2(demultiplexer_1_out2),
    .out3(demultiplexer_1_out3), .out4(demultiplexer_1_out4), .out5(demultiplexer_1_out5),
    .out6(demultiplexer_1_out6), .out7(demultiplexer_1_out7), .out8(demultiplexer_1_out8),
    .out9(demultiplexer_1_out9), .out10(demultiplexer_1_out10), .out11(demultiplexer_1_out11),
    .out12(demultiplexer_1_out12), .out13(demultiplexer_1_out13), .out14(demultiplexer_1_out14),
    .out15(demultiplexer_1_out15), .in(in_4), .sel(selecionando_Reg));  // open: en
  Register register_1 (.D(in_1), .en(demultiplexer_1_out8), .Q(register_1_q), .clk(in_2));  // open: clr
  Register register_2 (.D(in_1), .en(demultiplexer_1_out9), .Q(register_2_q), .clk(in_2));  // open: clr
  Register register_3 (.D(in_1), .en(demultiplexer_1_out0), .Q(register_3_q), .clk(in_2));  // open: clr
  Register register_4 (.D(in_1), .en(demultiplexer_1_out1), .Q(register_4_q), .clk(in_2));  // open: clr
  Multiplexer #(.select(4), .width(8)) multiplexer_1 (
    .in0(register_3_q), .in1(register_4_q), .in2(register_6_q), .in3(register_8_q), .in4(register_10_q),
    .in5(register_13_q), .in6(register_14_q), .in7(register_16_q), .in8(register_1_q), .in9(register_2_q),
    .in10(register_5_q), .in11(register_7_q), .in12(register_9_q), .in13(register_11_q),
    .in14(register_12_q), .in15(register_15_q), .out(out_7), .sel(in_5), .en(clock));
  Register register_5 (.D(in_1), .en(demultiplexer_1_out10), .Q(register_5_q), .clk(in_2));  // open: clr
  Register register_6 (.D(in_1), .en(demultiplexer_1_out2), .Q(register_6_q), .clk(in_2));  // open: clr
  Register register_7 (.D(in_1), .en(demultiplexer_1_out11), .Q(register_7_q), .clk(in_2));  // open: clr
  Register register_8 (.D(in_1), .en(demultiplexer_1_out3), .Q(register_8_q), .clk(in_2));  // open: clr
  Register register_9 (.D(in_1), .en(demultiplexer_1_out12), .Q(register_9_q), .clk(in_2));  // open: clr
  Register register_10 (.D(in_1), .en(demultiplexer_1_out4), .Q(register_10_q), .clk(in_2));  // open: clr
  Register register_11 (.D(in_1), .en(demultiplexer_1_out13), .Q(register_11_q), .clk(in_2));  // open: clr
  Register register_12 (.D(in_1), .en(demultiplexer_1_out14), .Q(register_12_q), .clk(in_2));  // open: clr
  Register register_13 (.D(in_1), .en(demultiplexer_1_out5), .Q(register_13_q), .clk(in_2));  // open: clr
  Register register_14 (.D(in_1), .en(demultiplexer_1_out6), .Q(register_14_q), .clk(in_2));  // open: clr
  Register register_15 (.D(in_1), .en(demultiplexer_1_out15), .Q(register_15_q), .clk(in_2));  // open: clr
  Register register_16 (.D(in_1), .en(demultiplexer_1_out7), .Q(register_16_q), .clk(in_2));  // open: clr

  // Notes on the sheet:
  //   Info
  //   Saída
endmodule
