// Logisim project SOMADOR - SISTEMAS DIGITAIS -2018.circ as structural Verilog: 1 circuit, main circuit main
module main (
  input  a0,
  input  a1,
  input  in_3,
  input  b0,
  input  b1,
  output s0,
  output s1,
  output Vai_1
);

  wire nand_1_out, nand_2_out, nand_3_out, nand_4_out, nand_5_out, xor_1_out, xor_2_out;

  xor xor_1 (xor_1_out, a0, b0);
  nand nand_1 (nand_1_out, a0, b0);
  xor xor_2 (xor_2_out, a1, b1);
  nand nand_2 (nand_2_out, a1, b1);
  xor xor_3 (s0, xor_1_out, in_3);
  nand nand_3 (nand_3_out, in_3, xor_1_out);
  xor xor_4 (s1, xor_2_out, nand_5_out);
  nand nand_4 (nand_4_out, nand_5_out, xor_2_out);
  nand nand_5 (nand_5_out, nand_3_out, nand_3_out, nand_1_out);
  nand nand_6 (Vai_1, nand_4_out, nand_4_out, nand_2_out);

  // Notes on the sheet:
  //   exemplo 00+01= 01
endmodule
