// Logisim project Somat.circ as structural Verilog: 4 circuits, main circuit BC
module BC (
  input  \Início ,
  input  Reset,
  input  Clock,
  input  Zero,
  output Set,
  output Dec,
  output Cac,
  output Rac,
  output Pronto
);

  wire and_1_out, and_2_out, and_3_out, and_4_out, and_5_out, or_1_out, or_2_out, s_r_ff_1_q, s_r_ff_1_qn,
       s_r_ff_2_q;

  or or_1 (or_1_out, and_2_out, and_3_out);
  or or_2 (or_2_out, and_4_out, and_5_out);
  and and_1 (and_1_out, s_r_ff_2_q, s_r_ff_1_qn);
  S_R_Flip_Flop s_r_ff_1 (
    .S(and_1_out), .clk(Clock), .R(s_r_ff_1_q), .Q(s_r_ff_1_q), .Qn(s_r_ff_1_qn), .reset(Reset));  // open: preset, en
  and and_2 (and_2_out, s_r_ff_1_q, s_r_ff_2_q);
  and and_3 (and_3_out, s_r_ff_1_qn, Pronto, \Início );
  S_R_Flip_Flop s_r_ff_2 (
    .S(or_1_out), .clk(Clock), .R(or_2_out), .Q(s_r_ff_2_q), .Qn(Pronto), .reset(Reset));  // open: preset, en
  and and_4 (and_4_out, s_r_ff_1_q, Pronto);
  and and_5 (and_5_out, s_r_ff_1_qn, s_r_ff_2_q, Zero);
  nor nor_1 (Rac, s_r_ff_1_q, s_r_ff_2_q);
  and and_6 (Cac, s_r_ff_1_q, s_r_ff_2_q);

  assign Dec = Cac;
  assign Set = Rac;
endmodule

module Somatorio (
  input  [7:0] Valor,
  input  \Início ,
  input  Clock,
  input  Reset,
  output [7:0] Soma,
  output Pronto,
  output Overflow
);

  wire bc_1_cac, bc_1_dec, bc_1_rac, bc_1_set, bo_1_zero;

  BC bc_1 (
    .\Início (\Início ), .Reset(Reset), .Clock(Clock), .Pronto(Pronto), .Set(bc_1_set), .Dec(bc_1_dec),
    .Cac(bc_1_cac), .Rac(bc_1_rac), .Zero(bo_1_zero));
  BO bo_1 (
    .Set(bc_1_set), .Dec(bc_1_dec), .Cac(bc_1_cac), .Rac(bc_1_rac), .Zero(bo_1_zero), .Overflow(Overflow),
    .Valor(Valor), .Soma(Soma), .Clock(Clock));
endmodule

module BO (
  input  [7:0] Valor,
  input  Set,
  input  Dec,
  input  Cac,
  input  Rac,
  input  Clock,
  output Zero,
  output Overflow,
  output [7:0] Soma
);

  wire [7:0] adder_1_out;

  Register register_1 (.D(adder_1_out), .en(Cac), .Q(Soma), .clk(Clock), .clr(Rac));
  Adder adder_1 (.a(Valor), .b(Soma), .out(adder_1_out), .cout(Overflow));  // open: cin
  Counter #(.width(3), .max('h4)) counter_1 (.count(Dec), .carry(Zero), .clk(Clock), .clr(Set));  // open: load, D, Q
endmodule

module Completo (
  input  [7:0] Valor,
  input  \Início ,
  input  Reset,
  output [7:0] Soma,
  output Pronto,
  output Overflow
);

  wire and_1_out, and_2_out, and_3_out, and_4_out, and_5_out, and_6_out, Clock_out, counter_1_carry,
       nor_1_out, or_1_out, or_2_out, s_r_ff_1_q, s_r_ff_1_qn, s_r_ff_2_q;
  wire [7:0] adder_1_out;

  Clock Clock (.out(Clock_out));
  or or_1 (or_1_out, and_2_out, and_3_out);
  or or_2 (or_2_out, and_4_out, and_5_out);
  and and_1 (and_1_out, s_r_ff_2_q, s_r_ff_1_qn);
  S_R_Flip_Flop s_r_ff_1 (
    .S(and_1_out), .clk(Clock_out), .R(s_r_ff_1_q), .Q(s_r_ff_1_q), .Qn(s_r_ff_1_qn), .reset(Reset));  // open: preset, en
  and and_2 (and_2_out, s_r_ff_1_q, s_r_ff_2_q);
  and and_3 (and_3_out, s_r_ff_1_qn, Pronto, \Início );
  S_R_Flip_Flop s_r_ff_2 (
    .S(or_1_out), .clk(Clock_out), .R(or_2_out), .Q(s_r_ff_2_q), .Qn(Pronto), .reset(Reset));  // open: preset, en
  and and_4 (and_4_out, s_r_ff_1_q, Pronto);
  and and_5 (and_5_out, s_r_ff_1_qn, s_r_ff_2_q, counter_1_carry);
  nor nor_1 (nor_1_out, s_r_ff_1_q, s_r_ff_2_q);
  and and_6 (and_6_out, s_r_ff_1_q, s_r_ff_2_q);
  Register register_1 (.D(adder_1_out), .en(and_6_out), .Q(Soma), .clk(Clock_out), .clr(nor_1_out));
  Adder adder_1 (.a(Valor), .b(Soma), .out(adder_1_out), .cout(Overflow));  // open: cin
  Counter #(.width(3), .max('h4)) counter_1 (
    .count(and_6_out), .carry(counter_1_carry), .clk(Clock_out), .clr(nor_1_out));  // open: load, D, Q
endmodule
